# Fritzing sketch petPRoject sensores salud (saved by Fritzing 0.9.3b)

parts:
  LCD1 = LCD screen
  LED7 = smd LED [color="Red (633nm)" package="1206 [SMD]"]  # not connected
  LED8 = LED - 5mm [color="Yellow (595nm)" package="5 mm [THT]"]  # not connected
  LED9 = LED - 5mm [color="Green (570nm)" package="5 mm [THT]"]  # not connected
  LED10 = LED - 5mm [color="Blue (430nm)" package="5 mm [THT]"]  # not connected
  U1 = SWITCH_SPDT [package=kps-1290]
  Componente2 = Gas Sensor Breakout Board
  Grove1 = Grove Light Sensor  # not connected
  U2 = MAX6675 [package=so08]
  R1 = Resistor [tolerance=±5% resistance=220 package="0603 [SMD]"]
  VCC1 = Battery block 9V
  R2 = Resistor [tolerance=±5% resistance=220 package="0603 [SMD]"]
  R3 = Resistor [tolerance=±5% resistance=220 package="0603 [SMD]"]
  R4 = Resistor [tolerance=±5% resistance=220 package="0603 [SMD]"]
  LED11 = smd LED [color="Red (633nm)" package="1206 [SMD]"]
  LED12 = LED - 5mm [color="Yellow (595nm)" package="5 mm [THT]"]
  LED13 = LED - 5mm [color="Green (570nm)" package="5 mm [THT]"]
  R5 = Resistor [tolerance=±5% resistance=220 package="0603 [SMD]"]
  R6 = Resistor [tolerance=±5% resistance=220 package="0603 [SMD]"]
  R7 = Resistor [tolerance=±5% resistance=220 package="0603 [SMD]"]
  LED14 = smd LED [color="Red (633nm)" package="1206 [SMD]"]
  LED15 = LED - 5mm [color="Yellow (595nm)" package="5 mm [THT]"]
  LED16 = LED - 5mm [color="Green (570nm)" package="5 mm [THT]"]
  R8 = Resistor [tolerance=±5% resistance=220 package="0603 [SMD]"]
  R9 = Resistor [tolerance=±5% resistance=220 package="0603 [SMD]"]
  R10 = Resistor [tolerance=±5% resistance=220 package="0603 [SMD]"]
  Componente3 = Arduino Mega ADK (Rev3)
  R11 = Rotary Potentiometer (Small) [maximum_resistance=100kΩ package=THT]

nets:
  VDD: LCD1.VDD, Componente3.5V
  N1: LCD1.V0, R11.wiper
  N2: LCD1.RS, Componente3.D8_PWM
  N3: LCD1.DB4, Componente3.D4_PWM
  N4: LCD1.DB5, Componente3.D5_PWM
  N5: LCD1.DB6, Componente3.D6_PWM
  N6: LCD1.DB7, Componente3.D7_PWM
  N7: U1.O, Componente3.VIN
  N8: Componente2.H1, Componente3.A3
  N9: Componente2.A1, Componente3.D10_PWM
  GND: Componente2.GND, VCC1.-, LED14.cathode, LED15.anode, LED16.anode, R8.Pin_0, R9.Pin_0, Componente3.GND
  N10: U2.T-, Componente3.A1
  N11: U2.T+, Componente3.A2
  N12: R1.Pin_1, Componente3.D49
  N13: R2.Pin_1, Componente3.D43
  N14: R3.Pin_1, Componente3.D45
  N15: R4.Pin_1, Componente3.D47
  N16: LED11.cathode, LED12.cathode, LED13.cathode
  N17: R5.Pin_1, Componente3.D37
  N18: R6.Pin_1, Componente3.D39
  N19: R7.Pin_1, Componente3.D41
  N20: R8.Pin_1, Componente3.D31
  N21: R9.Pin_1, Componente3.D33
  N22: R10.Pin_1, Componente3.D35

notes:
  GND
  VCC
  V0
  A0
  D0
  SDA
  SCL
  AFAYA PET PROJECT
